# Fritzing sketch exemplo2 (saved by Fritzing 0.9.2b)

parts:
  Componente1 = Arduino Uno (Rev3)
  J1 = Basic Servo

nets:
  N1: Componente1.D3_PWM, J1.pulse
  5V: Componente1.5V, J1.vcc
  GND: Componente1.GND, J1.gnd

// code stored in the sketch: img.ino
#include <Servo.h>
 
Servo motor;
void setup() { 
 motor.attach(3);
} 

void loop() { 
 int i;
  for(i=0;i<180;i++) {
    motor.write(i); 
    delay(10); 
 }
  delay(1000);
  for(i=180;i>0;i--) {
    motor.write(i); 
    delay(10); 
 }
 delay(1000);
}
